# Fritzing sketch Overview (saved by Fritzing 0.9.3b)
breadboards: 1

parts:
  U2 = ESP32S-HiLetgo [part_number=ESP32S-HiLetgo]
  R5 = Resistor [tolerance=±5% resistance=4.7k package="1206 [SMD]"]
  GY-NEO6MV4 = SUP500F [package=sup500f]
  R6 = Resistor [tolerance=±5% resistance=10k package="1206 [SMD]"]
  IC2 = L293D [package=THT]
  GSM_SIM_GPSR_SMS_SIM900_SIM2 = SIM800L [package=THT]
  Part3 = Tri-Axis Gyro Breakout - L3G4200D
  Part4 = Arduino Micro (Rev3)
  VCC4 = 4 x AAA Battery Mount
  M5 = DC Motor
  M6 = DC Motor
  L298N3 = L298N DC motor driver

nets:
  N1: U2.3.3, GY-NEO6MV4.TX-O, Part3.VCC
  N2: U2.EN, L298N3.ENB
  N3: U2.GPIO36, L298N3.IN4
  N4: U2.GPIO39, L298N3.IN3
  N5: U2.GPIO34, L298N3.IN2
  N6: U2.GPIO32, L298N3.IN1
  N7: U2.GPIO33, L298N3.ENA
  N8: U2.GPIO25, Part3.SCL
  N9: U2.GPIO26, Part3.SDA
  GND: U2.GND, GY-NEO6MV4.RX-I, R6.Pin_1, Part3.GND, VCC4.-, L298N3.GND
  N10: U2.GPIO16, GY-NEO6MV4.VCC
  N11: U2.GPIO17, R5.Pin_0
  N12: R5.Pin_1, GY-NEO6MV4.GND, R6.Pin_0
  N13: IC2.Enable_1, IC2.+V
  N14: IC2.In_1, IC2.In_4
  N15: IC2.Out_1_(_Controlled_by_Enable_1_), IC2.Out_4_(_Controlled_by_Enable_2_)
  N16: IC2.Out_2_(_Controlled_by_Enable_1_), IC2.Out_3_(_Controlled_by_Enable_2_)
  N17: IC2.In_2, IC2.In_3
  N18: IC2.+Vmotor, IC2.Enable_2
  N19: GSM_SIM_GPSR_SMS_SIM900_SIM2.GND, Part4.RESET
  N20: GSM_SIM_GPSR_SMS_SIM900_SIM2.SIM_TXD, Part4.D7
  N21: GSM_SIM_GPSR_SMS_SIM900_SIM2.SIM_RXD, Part4.D8_PWM/A8
  N22: VCC4.+, L298N3.5V
  N23: M5.pin_1, L298N3.OUT4
  N24: M5.pin_2, L298N3.OUT3
  N25: M6.pin_1, L298N3.OUT2
  N26: M6.pin_2, L298N3.OUT1

notes:
  GND: Black
  VCC: Red
  RX: Yellow
  TX: Green
  Pin 7 is being set as RX and 8 as TX

custom parts:
  ESP32S-HiLetgo: HiLetgo ESP-WROOM-32 ESP32 ESP-32S Development Board 2.4GHz Dual-Mode WiFi + Bluetooth Dual Cores Microcontroller The ESP32 integrated with Antenna switches, RF Balun, power amplifiers, low-noise amplifiers, filters, and management modules, and the entire solution occupies the least area of PCB. 2.4 GHz Wi-Fi plus Bluetooth dual-mode chip, with TSMC Ultra-low power consumption 40nm technology,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
  L298N DC motor driver: 2x DC motor driver with 78M05 positive voltage regulator (7..35 V) L298N: max 46 V, 2 A Set 5 V Enable jumper to enable 5 V regultor (needed for the L298N) and +5 V output at screw terminal or supply external +5 V at screw terminal Set ENA and/or ENB to +5 V to enable motor permanently or supply ENA and/or ENB with PWM signal IN1 and IN2 set rotation directory for motor A (OUT1/OUT2) IN2 and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
