# Fritzing sketch Motor (saved by Fritzing 0.9.3b)
breadboards: 1

parts:
  U1 = ESP32S-HiLetgo [part_number=ESP32S-HiLetgo]
  L298N1 = L298N DC motor driver
  VCC2 = 4 x AAA Battery Mount
  M1 = DC Motor  # not connected
  M2 = DC Motor  # not connected
  IC1 = L293D [package=THT]

nets:
  N1: U1.GPIO35, L298N1.ENB
  N2: U1.GPIO32, L298N1.IN4
  N3: U1.GPIO33, L298N1.IN3
  N4: U1.GPIO25, L298N1.IN2
  N5: U1.GPIO26, L298N1.IN1
  N6: U1.GPIO27, L298N1.ENA
  N7: U1.GND, VCC2.-
  N8: IC1.Enable_1, IC1.+V
  N9: IC1.In_1, IC1.In_4
  N10: IC1.Out_1_(_Controlled_by_Enable_1_), IC1.Out_4_(_Controlled_by_Enable_2_)
  N11: IC1.Out_2_(_Controlled_by_Enable_1_), IC1.Out_3_(_Controlled_by_Enable_2_)
  N12: IC1.In_2, IC1.In_3
  N13: IC1.+Vmotor, IC1.Enable_2

custom parts:
  ESP32S-HiLetgo: HiLetgo ESP-WROOM-32 ESP32 ESP-32S Development Board 2.4GHz Dual-Mode WiFi + Bluetooth Dual Cores Microcontroller The ESP32 integrated with Antenna switches, RF Balun, power amplifiers, low-noise amplifiers, filters, and management modules, and the entire solution occupies the least area of PCB. 2.4 GHz Wi-Fi plus Bluetooth dual-mode chip, with TSMC Ultra-low power consumption 40nm technology,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
  L298N DC motor driver: 2x DC motor driver with 78M05 positive voltage regulator (7..35 V) L298N: max 46 V, 2 A Set 5 V Enable jumper to enable 5 V regultor (needed for the L298N) and +5 V output at screw terminal or supply external +5 V at screw terminal Set ENA and/or ENB to +5 V to enable motor permanently or supply ENA and/or ENB with PWM signal IN1 and IN2 set rotation directory for motor A (OUT1/OUT2) IN2 and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
