# Fritzing sketch NEO6M (saved by Fritzing 0.9.3b)
breadboards: 1

parts:
  U1 = ESP32S-HiLetgo [part_number=ESP32S-HiLetgo]
  GY-NEO6MV3 = SUP500F [package=sup500f]
  R3 = Resistor [tolerance=±5% resistance=4.7k package="1206 [SMD]"]
  R4 = Resistor [tolerance=±5% resistance=10k package="1206 [SMD]"]

nets:
  N1: U1.3.3, GY-NEO6MV3.TX-O
  N2: U1.GND, GY-NEO6MV3.RX-I, R4.Pin_1
  N3: U1.GPIO17, R3.Pin_0
  N4: GY-NEO6MV3.GND, R3.Pin_1, R4.Pin_0

notes:
  GND: Black
  VCC: Red
  RX: Yellow
  TX: Green

custom parts:
  ESP32S-HiLetgo: HiLetgo ESP-WROOM-32 ESP32 ESP-32S Development Board 2.4GHz Dual-Mode WiFi + Bluetooth Dual Cores Microcontroller The ESP32 integrated with Antenna switches, RF Balun, power amplifiers, low-noise amplifiers, filters, and management modules, and the entire solution occupies the least area of PCB. 2.4 GHz Wi-Fi plus Bluetooth dual-mode chip, with TSMC Ultra-low power consumption 40nm technology,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
