# Fritzing sketch Navigation (saved by Fritzing 0.9.3b)
breadboards: 1

parts:
  U1 = ESP32S-HiLetgo [part_number=ESP32S-HiLetgo]
  GY1 = GY-80
  R5 = Resistor [tolerance=±5% resistance=4.7k package="1206 [SMD]"]
  R6 = Resistor [tolerance=±5% resistance=10k package="1206 [SMD]"]
  GY-NEO6MV5 = SUP500F [package=sup500f]

nets:
  N1: U1.3.3, GY1.VCC_3.3V, GY-NEO6MV5.TX-O
  GND: U1.GND, GY1.GND, R6.Pin_1, GY-NEO6MV5.RX-I, GY-NEO6MV5.GND
  N2: U1.GPIO16, GY-NEO6MV5.VCC
  N3: U1.GPIO17, R5.Pin_0
  N4: U1.GPIO21, GY1.SDA
  N5: U1.GPIO22, GY1.SCL
  N6: R5.Pin_1, R6.Pin_0

notes:
  GND: Black
  VCC: Red
  RX: Yellow
  TX: Green

custom parts:
  ESP32S-HiLetgo: HiLetgo ESP-WROOM-32 ESP32 ESP-32S Development Board 2.4GHz Dual-Mode WiFi + Bluetooth Dual Cores Microcontroller The ESP32 integrated with Antenna switches, RF Balun, power amplifiers, low-noise amplifiers, filters, and management modules, and the entire solution occupies the least area of PCB. 2.4 GHz Wi-Fi plus Bluetooth dual-mode chip, with TSMC Ultra-low power consumption 40nm technology,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
  GY-80: Placa GY-80 basada en conjunto de giroscopios L3G4200D + acelerómetros ADXL345 + magnetómetro HMC5883L + sensor barométrico BMP085
