# Fritzing sketch sim900A (saved by Fritzing 0.9.3b)

parts:
  GSM_SIM_GPSR_SMS_SIM900_SIM1 = SIM800L [package=THT]
  Part1 = Arduino Uno (Rev3)

nets:
  GND: GSM_SIM_GPSR_SMS_SIM900_SIM1.GND, Part1.GND
  N1: GSM_SIM_GPSR_SMS_SIM900_SIM1.SIM_TXD, Part1.D7
  N2: GSM_SIM_GPSR_SMS_SIM900_SIM1.SIM_RXD, Part1.D8

notes:
  Pin 7 is being set as RX and 8 as TX
